# Fritzing sketch rfid_player_wiring (saved by Fritzing 0.9.3b)
breadboards: 1

parts:
  Raspberry_Pi_1 = Raspberry Pi 3 [part_number=RPI-3-V1.2]
  S1 = Pushbutton [part_number=Play package="[THT]"]
  S2 = Pushbutton [part_number="volume up" package="[THT]"]
  R1 = Resistor [tolerance=±5% resistance=330 package="2010 [SMD]"]
  S3 = Pushbutton [part_number="volume down" package="[THT]"]
  S4 = Pushbutton [part_number="next track" package="[THT]"]
  S5 = Pushbutton [part_number="prev track" package="[THT]"]
  LED2 = smd LED [color="Green (555nm)" package="1206 [SMD]"]

nets:
  N1: Raspberry_Pi_1.GPIO27, S3.Pin_3, S3.Pin_4
  N2: Raspberry_Pi_1.GND, S1.Pin_1, S1.Pin_2, S2.Pin_1, S2.Pin_2, R1.Pin_1, S3.Pin_1, S3.Pin_2, S4.Pin_1, S4.Pin_2, S5.Pin_1, S5.Pin_2
  N3: Raspberry_Pi_1.GPIO5, S4.Pin_3, S4.Pin_4
  N4: Raspberry_Pi_1.GPIO6, S5.Pin_3, S5.Pin_4
  N5: Raspberry_Pi_1.GPIO24, S2.Pin_3, S2.Pin_4
  N6: Raspberry_Pi_1.GPIO23, S1.Pin_3, S1.Pin_4
  N7: Raspberry_Pi_1.GPIO14, LED2.cathode
  N8: R1.Pin_0, LED2.anode

notes:
  play/pause
  volume ⬆
  volume ⬇️
  next track
  prev track
